# Fritzing sketch wiring (saved by Fritzing 0.9.3b)
breadboards: 1

parts:
  Part1 = Arduino Uno (Rev3) - ICSP
  S1 = H-Bridge with L298N
  M1 = Stepper Motor - Unipolar  # not connected
  S3 = Square Pushbutton
  JP1 = Header 4 [package=molex-1x4_lock]
  LED1 = smd LED [color="Red (633nm)" package="0603 [SMD]"]
  R1 = Resistor [tolerance=±5% resistance=220 package="2512 [SMD]"]
  S4 = Pushbutton [package="[SMD]"]
  S5 = Pushbutton [package="[SMD]"]

nets:
  N1: Part1.A0, R1.Pin_1
  N2: Part1.A1, S4.Pin_1, S4.Pin_2
  N3: Part1.A2, S5.Pin_1, S5.Pin_2
  N4: Part1.ICSP_MOSI, Part1.D11_PWM/MOSI, S1.IN4
  GND: Part1.GND, S1.GND, S3.leg1, JP1.1, LED1.cathode, S4.Pin_3, S5.Pin_3, S5.Pin_4
  N5: Part1.D8, S1.IN1
  N6: Part1.D9_PWM, S1.IN2
  N7: Part1.D10_PWM/SS, S1.IN3
  N8: Part1.D2, JP1.3
  N9: Part1.D3_PWM, JP1.2
  N10: Part1.D4, S3.leg0
  N11: Part1.D5_PWM, S1.ENB
  N12: Part1.D6_PWM, S1.ENA
  N13: Part1.5V, JP1.4
  VIN: Part1.VIN, S1.12V

notes:
  8 wires from Bipolar stepper motor
  1- connect BLU and RED/WHT
  2- connect GRN and BLK/WHT
  BLU/WHT, BLU, RED/WHT, RED, GRN/WHT, GRN, BLK/WHT, BLK
  keep jumper settings on bridge module
  DC 12V input from 348W, power module
  From HEDS quadrature encoder
  We will use interrupt in order to detect encoder pulses.
  1- GND, 2-CHNB, 3-CHNA, 4-VCC ,
  Resistor for LED drive is 220ohm
  It does not need debounce circuit, because we can use debounce logic in software.
  GT2 belt and 20-tooth pulley
  Encoder & Film
  Microswitches for detecting start and end edge.
  1- start, 2-end
  http://www.ebay.com/itm/10-x-Micro-Limit-Switch-Long-Straight-Hinge-Lever-SPDT-Snap-Action-LOT-Black/321590790999?_trkparms=aid%3D222007%26algo%3DSIM.MBE%26ao%3D1%26asc%3D20160908110712%26meid%3Dd248f9e58a0a4597b4c3e5114c3d38d2%26pid%3D100677%26rk%3D2%26rkt%3D30%26mehot%3Dlo%26sd%3D253199513457&_trksid=p2385738.c100677.m4598

custom parts:
  H-Bridge with L298N: h-bridge
